# Fritzing sketch RightHandMatrixKeyboard (saved by Fritzing 0.9.2b)
breadboards: 1

parts:
  Teensy1 = Teensy 2.0  # not connected
  S1 = Cherry MX Keyswitch
  S29 = Cherry MX Keyswitch
  S30 = Cherry MX Keyswitch
  S31 = Cherry MX Keyswitch
  S32 = Cherry MX Keyswitch
  S33 = Cherry MX Keyswitch
  S34 = Cherry MX Keyswitch
  S35 = Cherry MX Keyswitch
  S36 = Cherry MX Keyswitch
  S37 = Cherry MX Keyswitch
  S38 = Cherry MX Keyswitch
  S39 = Cherry MX Keyswitch
  S40 = Cherry MX Keyswitch
  S41 = Cherry MX Keyswitch
  S42 = Cherry MX Keyswitch
  S43 = Cherry MX Keyswitch
  S44 = Cherry MX Keyswitch
  S45 = Cherry MX Keyswitch
  S46 = Cherry MX Keyswitch
  S47 = Cherry MX Keyswitch
  S48 = Cherry MX Keyswitch
  S49 = Cherry MX Keyswitch
  S50 = Cherry MX Keyswitch
  S51 = Cherry MX Keyswitch
  S52 = Cherry MX Keyswitch
  S53 = Cherry MX Keyswitch
  S54 = Cherry MX Keyswitch
  S55 = Cherry MX Keyswitch
  S56 = Cherry MX Keyswitch
  S57 = Cherry MX Keyswitch
  S58 = Cherry MX Keyswitch
  S59 = Cherry MX Keyswitch
  S60 = Cherry MX Keyswitch
  D1 = Diode [package=diode-1n4148]  # not connected

nets:
  N1: S1.pin_2, S1.pin_3
  N2: S1.pin_4, S1.pin_5
  N3: S29.pin_2, S29.pin_3
  N4: S29.pin_4, S29.pin_5
  N5: S30.pin_2, S30.pin_3
  N6: S30.pin_4, S30.pin_5
  N7: S31.pin_2, S31.pin_3
  N8: S31.pin_4, S31.pin_5
  N9: S32.pin_2, S32.pin_3
  N10: S32.pin_4, S32.pin_5
  N11: S33.pin_2, S33.pin_3
  N12: S33.pin_4, S33.pin_5
  N13: S34.pin_2, S34.pin_3
  N14: S34.pin_4, S34.pin_5
  N15: S35.pin_2, S35.pin_3
  N16: S35.pin_4, S35.pin_5
  N17: S36.pin_2, S36.pin_3
  N18: S36.pin_4, S36.pin_5
  N19: S37.pin_2, S37.pin_3
  N20: S37.pin_4, S37.pin_5
  N21: S38.pin_2, S38.pin_3
  N22: S38.pin_4, S38.pin_5
  N23: S39.pin_2, S39.pin_3
  N24: S39.pin_4, S39.pin_5
  N25: S40.pin_2, S40.pin_3
  N26: S40.pin_4, S40.pin_5
  N27: S41.pin_2, S41.pin_3
  N28: S41.pin_4, S41.pin_5
  N29: S42.pin_2, S42.pin_3
  N30: S42.pin_4, S42.pin_5
  N31: S43.pin_2, S43.pin_3
  N32: S43.pin_4, S43.pin_5
  N33: S44.pin_2, S44.pin_3
  N34: S44.pin_4, S44.pin_5
  N35: S45.pin_2, S45.pin_3
  N36: S45.pin_4, S45.pin_5
  N37: S46.pin_2, S46.pin_3
  N38: S46.pin_4, S46.pin_5
  N39: S47.pin_2, S47.pin_3
  N40: S47.pin_4, S47.pin_5
  N41: S48.pin_2, S48.pin_3
  N42: S48.pin_4, S48.pin_5
  N43: S49.pin_2, S49.pin_3
  N44: S49.pin_4, S49.pin_5
  N45: S50.pin_2, S50.pin_3
  N46: S50.pin_4, S50.pin_5
  N47: S51.pin_2, S51.pin_3
  N48: S51.pin_4, S51.pin_5
  N49: S52.pin_2, S52.pin_3
  N50: S52.pin_4, S52.pin_5
  N51: S53.pin_2, S53.pin_3
  N52: S53.pin_4, S53.pin_5
  N53: S54.pin_2, S54.pin_3
  N54: S54.pin_4, S54.pin_5
  N55: S55.pin_2, S55.pin_3
  N56: S55.pin_4, S55.pin_5
  N57: S56.pin_2, S56.pin_3
  N58: S56.pin_4, S56.pin_5
  N59: S57.pin_2, S57.pin_3
  N60: S57.pin_4, S57.pin_5
  N61: S58.pin_2, S58.pin_3
  N62: S58.pin_4, S58.pin_5
  N63: S59.pin_2, S59.pin_3
  N64: S59.pin_4, S59.pin_5
  N65: S60.pin_2, S60.pin_3
  N66: S60.pin_4, S60.pin_5
